// Digital circuit ALU.dig as structural Verilog
module ALU (
  input  En,
  input  [3:0] Opcode,
  input  [15:0] A,
  input  [15:0] B,
  input  CLK,
  input  Carry_In,
  input  Borrow_In,
  output [15:0] Sum,
  output Carry_Out,
  output Borrow_Out,
  output [15:0] Sub,
  output [15:0] mul_low,
  output [15:0] mul_high,
  output [15:0] AND,
  output [15:0] XOR,
  output [15:0] OR,
  output [15:0] Not,
  output [15:0] SAR,
  output [15:0] SHR,
  output [15:0] SHL,
  output [15:0] SLT,
  output LSU_EN
);

  wire _16_bitmuxwithenablepin_1_q0, _16_bitmuxwithenablepin_1_q1, _16_bitmuxwithenablepin_1_q2,
       _16_bitmuxwithenablepin_1_q3, _16_bitmuxwithenablepin_1_q4, _16_bitmuxwithenablepin_1_q5,
       _16_bitmuxwithenablepin_1_q6, _16_bitmuxwithenablepin_1_q7, _16_bitmuxwithenablepin_1_q8,
       _16_bitmuxwithenablepin_1_q9, _16_bitmuxwithenablepin_1_q10, _16_bitmuxwithenablepin_1_q11,
       _16_bitmuxwithenablepin_1_q12, _16_bitmuxwithenablepin_1_q13, _16_bitmuxwithenablepin_1_q14,
       alu_regctrl_1_q_0, alu_regctrl_1_q_1, alu_regctrl_1_q_2, alu_regctrl_1_q_3, alu_regctrl_1_q_4,
       alu_regctrl_1_q_5, alu_regctrl_1_q_6, alu_regctrl_1_q_7, alu_regctrl_1_q_8, alu_regctrl_1_q_9,
       alu_regctrl_1_q_a, alu_regctrl_1_q_b, alu_regctrl_1_rst, and_1_out, not_1_out, not_2_out, not_3_out,
       not_6_out, not_7_out, not_10_out, not_12_out, not_14_out, not_16_out, not_18_out, not_20_out,
       not_22_out, not_24_out, not_26_out, not_28_out, not_30_out, not_32_out, not_34_out, not_35_out,
       not_36_out, not_38_out, not_39_out, not_40_out, not_42_out, not_43_out, not_44_out, not_45_out;
  wire [4:0] _5_bit_reg_2_q, _5_bit_reg_3_q, _5_bit_reg_q, alu_regrst_2_q;
  wire [15:0] alu_regrst_1_q, mul_2_mul, undriven, undriven_2, undriven_3, undriven_4, undriven_5,
       undriven_6, undriven_7, undriven_8, undriven_9, undriven_10, undriven_11, undriven_12, undriven_13,
       undriven_14, undriven_15, undriven_16, undriven_17, undriven_18, undriven_19, undriven_20;
  wire [15:5] alu_regrst_2_q_2;
  wire [31:16] mul_1_mul;

  not not_1 (not_1_out, LSU_EN);
  and and_1 (and_1_out, not_1_out, En);
  _16_BitMuxWithEnablePin _16_bitmuxwithenablepin_1 (
    .EN(En), .Sel_4Bit(Opcode), .Q0(_16_bitmuxwithenablepin_1_q0), .Q1(_16_bitmuxwithenablepin_1_q1),
    .Q2(_16_bitmuxwithenablepin_1_q2), .Q3(_16_bitmuxwithenablepin_1_q3), .Q4(_16_bitmuxwithenablepin_1_q4),
    .Q5(_16_bitmuxwithenablepin_1_q5), .Q6(_16_bitmuxwithenablepin_1_q6), .Q7(_16_bitmuxwithenablepin_1_q7),
    .Q8(_16_bitmuxwithenablepin_1_q8), .Q9(_16_bitmuxwithenablepin_1_q9),
    .Q10(_16_bitmuxwithenablepin_1_q10), .Q11(_16_bitmuxwithenablepin_1_q11),
    .Q12(_16_bitmuxwithenablepin_1_q12), .Q13(_16_bitmuxwithenablepin_1_q13),
    .Q14(_16_bitmuxwithenablepin_1_q14), .Q15(LSU_EN));
  ALU_RegCtrl alu_regctrl_1 (
    .IsEn__MUX(and_1_out), .CLK(CLK), ._0x0(_16_bitmuxwithenablepin_1_q0),
    ._0x1(_16_bitmuxwithenablepin_1_q1), ._0x2(_16_bitmuxwithenablepin_1_q2),
    ._0x3(_16_bitmuxwithenablepin_1_q3), ._0x4(_16_bitmuxwithenablepin_1_q4),
    ._0x5(_16_bitmuxwithenablepin_1_q5), ._0x6(_16_bitmuxwithenablepin_1_q6),
    ._0x7(_16_bitmuxwithenablepin_1_q7), ._0x8(_16_bitmuxwithenablepin_1_q8),
    ._0x9(_16_bitmuxwithenablepin_1_q9), ._0xA(_16_bitmuxwithenablepin_1_q10),
    ._0xB(_16_bitmuxwithenablepin_1_q11), ._0xC(_16_bitmuxwithenablepin_1_q12),
    ._0xD(_16_bitmuxwithenablepin_1_q13), ._0xE(_16_bitmuxwithenablepin_1_q14), ._0xF(LSU_EN),
    .Q_0(alu_regctrl_1_q_0), .Q_1(alu_regctrl_1_q_1), .Q_2(alu_regctrl_1_q_2), .Q_3(alu_regctrl_1_q_3),
    .Q_4(alu_regctrl_1_q_4), .Q_5(alu_regctrl_1_q_5), .Q_6(alu_regctrl_1_q_6), .Q_7(alu_regctrl_1_q_7),
    .Q_8(alu_regctrl_1_q_8), .Q_9(alu_regctrl_1_q_9), .Q_A(alu_regctrl_1_q_a), .Q_B(alu_regctrl_1_q_b),
    .RST(alu_regctrl_1_rst));  // open: Q_C, Q_D, Q_E, Q_F
  ALU_RegRST alu_regrst_1 (.D(A), .RST(alu_regctrl_1_rst), .Q(alu_regrst_1_q));
  ALU_RegRST alu_regrst_2 (.D(B), .RST(alu_regctrl_1_rst), .Q({alu_regrst_2_q_2, alu_regrst_2_q}));
  not not_2 (not_2_out, CLK);
  not not_3 (not_3_out, CLK);
  // _16_BitRegister _16_bitregister_1: pin names not known; wires that end beside it: alu_regrst_1_q, alu_regctrl_1_q_0
  // Not not_4 has open pins: in=not_2_out, out=open
  // _16_BitRegister _16_bitregister_2: pin names not known; wires that end beside it: {alu_regrst_2_q_2, alu_regrst_2_q}, alu_regctrl_1_q_0
  // Not not_5 has open pins: in=not_3_out, out=open
  Add #(.Bits(16)) add_1 (.a(undriven), .b(undriven_2), .c_i(Carry_In), .s(Sum), .c_o(Carry_Out));
  not not_6 (not_6_out, CLK);
  not not_7 (not_7_out, CLK);
  // _16_BitRegister _16_bitregister_3: pin names not known; wires that end beside it: alu_regrst_1_q, alu_regctrl_1_q_1
  // Not not_8 has open pins: in=not_6_out, out=open
  // _16_BitRegister _16_bitregister_4: pin names not known; wires that end beside it: {alu_regrst_2_q_2, alu_regrst_2_q}, alu_regctrl_1_q_1
  // Not not_9 has open pins: in=not_7_out, out=open
  Sub #(.Bits(16)) sub_1 (.a(undriven_3), .b(undriven_4), .c_i(Borrow_In), .s(Sub), .c_o(Borrow_Out));
  not not_10 (not_10_out, CLK);
  // Not not_11 has open pins: in=not_10_out, out=open
  not not_12 (not_12_out, CLK);
  // Not not_13 has open pins: in=not_12_out, out=open
  // _16_BitRegister _16_bitregister_5: pin names not known; wires that end beside it: alu_regrst_1_q, alu_regctrl_1_q_2
  // _16_BitRegister _16_bitregister_6: pin names not known; wires that end beside it: {alu_regrst_2_q_2, alu_regrst_2_q}, alu_regctrl_1_q_2
  Mul #(.Signed("true"), .Bits(16)) mul_1 (.a(undriven_5), .b(undriven_6), .mul({mul_1_mul, mul_low}));
  not not_14 (not_14_out, CLK);
  // Not not_15 has open pins: in=not_14_out, out=open
  not not_16 (not_16_out, CLK);
  // Not not_17 has open pins: in=not_16_out, out=open
  // _16_BitRegister _16_bitregister_7: pin names not known; wires that end beside it: alu_regrst_1_q, alu_regctrl_1_q_3
  // _16_BitRegister _16_bitregister_8: pin names not known; wires that end beside it: {alu_regrst_2_q_2, alu_regrst_2_q}, alu_regctrl_1_q_3
  Mul #(.Signed("true"), .Bits(16)) mul_2 (.a(undriven_7), .b(undriven_8), .mul({mul_high, mul_2_mul}));
  not not_18 (not_18_out, CLK);
  // Not not_19 has open pins: in=not_18_out, out=open
  not not_20 (not_20_out, CLK);
  // Not not_21 has open pins: in=not_20_out, out=open
  // _16_BitRegister _16_bitregister_9: pin names not known; wires that end beside it: alu_regrst_1_q, alu_regctrl_1_q_4
  // _16_BitRegister _16_bitregister_10: pin names not known; wires that end beside it: {alu_regrst_2_q_2, alu_regrst_2_q}, alu_regctrl_1_q_4
  _16_BitAndOP _16_bitandop_1 (.A(undriven_9), .B(undriven_10), .Q(AND));
  not not_22 (not_22_out, CLK);
  // Not not_23 has open pins: in=not_22_out, out=open
  not not_24 (not_24_out, CLK);
  // Not not_25 has open pins: in=not_24_out, out=open
  // _16_BitRegister _16_bitregister_11: pin names not known; wires that end beside it: alu_regrst_1_q, alu_regctrl_1_q_5
  // _16_BitRegister _16_bitregister_12: pin names not known; wires that end beside it: {alu_regrst_2_q_2, alu_regrst_2_q}, alu_regctrl_1_q_5
  _16_BitXorOP _16_bitxorop_1 (.A(undriven_11), .B(undriven_12), .Q(XOR));
  not not_26 (not_26_out, CLK);
  // Not not_27 has open pins: in=not_26_out, out=open
  not not_28 (not_28_out, CLK);
  // Not not_29 has open pins: in=not_28_out, out=open
  // _16_BitRegister _16_bitregister_13: pin names not known; wires that end beside it: alu_regrst_1_q, alu_regctrl_1_q_6
  // _16_BitRegister _16_bitregister_14: pin names not known; wires that end beside it: {alu_regrst_2_q_2, alu_regrst_2_q}, alu_regctrl_1_q_6
  _16_BitOrOP _16_bitorop_1 (.A(undriven_13), .B(undriven_14), .Q(OR));
  not not_30 (not_30_out, CLK);
  // _16_BitRegister _16_bitregister_15: pin names not known; wires that end beside it: alu_regrst_1_q, alu_regctrl_1_q_7
  // Not not_31 has open pins: in=not_30_out, out=open
  _16_BitNotOP _16_bitnotop_1 (.D(undriven_15), .Q(Not));
  not not_32 (not_32_out, CLK);
  // Not not_33 has open pins: in=not_32_out, out=open
  not not_34 (not_34_out, CLK);
  not not_35 (not_35_out, not_34_out);
  // _16_BitRegister _16_bitregister_16: pin names not known; wires that end beside it: alu_regrst_1_q, alu_regctrl_1_q_8
  Register #(.Bits(5)) _5_bit_reg (.D(alu_regrst_2_q), .C(not_35_out), .en(alu_regctrl_1_q_8), .Q(_5_bit_reg_q));
  BarrelShifter #(.Bits(16), .barrelShifterMode("arithmetic"), .direction("right")) barrelshifter_1 (
    .in(undriven_16), .shift(_5_bit_reg_q), .out(SAR));
  not not_36 (not_36_out, CLK);
  // Not not_37 has open pins: in=not_36_out, out=open
  not not_38 (not_38_out, CLK);
  not not_39 (not_39_out, not_38_out);
  // _16_BitRegister _16_bitregister_17: pin names not known; wires that end beside it: alu_regrst_1_q, alu_regctrl_1_q_9
  Register #(.Bits(5)) _5_bit_reg_2 (.D(alu_regrst_2_q), .C(not_39_out), .en(alu_regctrl_1_q_9), .Q(_5_bit_reg_2_q));
  BarrelShifter #(.Bits(16), .direction("right")) barrelshifter_2 (.in(undriven_17), .shift(_5_bit_reg_2_q), .out(SHR));
  not not_40 (not_40_out, CLK);
  // Not not_41 has open pins: in=not_40_out, out=open
  not not_42 (not_42_out, CLK);
  not not_43 (not_43_out, not_42_out);
  // _16_BitRegister _16_bitregister_18: pin names not known; wires that end beside it: alu_regrst_1_q, alu_regctrl_1_q_a
  Register #(.Bits(5)) _5_bit_reg_3 (.D(alu_regrst_2_q), .C(not_43_out), .en(alu_regctrl_1_q_a), .Q(_5_bit_reg_3_q));
  BarrelShifter #(.Bits(16)) barrelshifter_3 (.in(undriven_18), .shift(_5_bit_reg_3_q), .out(SHL));
  not not_44 (not_44_out, CLK);
  not not_45 (not_45_out, CLK);
  // _16_BitRegister _16_bitregister_19: pin names not known; wires that end beside it: alu_regrst_1_q, alu_regctrl_1_q_b
  // Not not_46 has open pins: in=not_44_out, out=open
  // _16_BitRegister _16_bitregister_20: pin names not known; wires that end beside it: {alu_regrst_2_q_2, alu_regrst_2_q}, alu_regctrl_1_q_b
  // Not not_47 has open pins: in=not_45_out, out=open
  Comparator comparator_1 (.a(undriven_19[0]), .b(undriven_20[0]), .lt(SLT[0]));  // open: gt, eq
  // Pins of 1 and 16 bits meet at undriven_19
  // Pins of 1 and 16 bits meet at undriven_20
  // Pins of 1 and 16 bits meet at SLT
endmodule
