// Digital circuit RegisterFile.dig as structural Verilog
module RegisterFile (
  input  CLK,
  input  [15:0] D,
  input  [3:0] in_4,
  input  [3:0] in_5,
  input  [3:0] IO_InSel,
  input  [3:0] IO_OutSel,
  input  [15:0] in_10,
  input  in_11,
  input  [15:0] SetMod_IO,
  output [15:0] out_1,
  output GPIO_OUT0x0,
  output GPIO_DataOUT,
  output [15:0] out_12,
  output GPIO_OUT0x1,
  output GPIO_OUT0x2,
  output GPIO_OUT0x3,
  output GPIO_OUT0x4,
  output GPIO_OUT0x5,
  output GPIO_OUT0x6,
  output GPIO_OUT0x7,
  output GPIO_OUT0x8,
  output GPIO_OUT0x9,
  output GPIO_OUT0xA,
  output GPIO_OUT0xB,
  output GPIO_OUT0xC,
  output GPIO_OUT0xD,
  output GPIO_OUT0xE,
  output GPIO_OUT0xF
);

  wire d_ff_1_q, decoder_2_out_0, decoder_2_out_1, decoder_2_out_2, decoder_2_out_3, decoder_2_out_4,
       decoder_2_out_5, decoder_2_out_6, decoder_2_out_7, decoder_2_out_8, decoder_2_out_9, decoder_2_out_10,
       decoder_2_out_11, decoder_2_out_12, decoder_2_out_13, decoder_2_out_14, decoder_2_out_15,
       decoder_3_out_0, decoder_3_out_1, decoder_3_out_2, decoder_3_out_3, decoder_3_out_4, decoder_3_out_5,
       decoder_3_out_6, decoder_3_out_7, decoder_3_out_8, decoder_3_out_9, decoder_3_out_10,
       decoder_3_out_11, decoder_3_out_12, decoder_3_out_13, decoder_3_out_14, decoder_3_out_15,
       register_1_q, register_2_q, register_3_q, register_4_q, register_13_q, register_14_q, register_15_q,
       register_16_q, register_25_q, register_26_q, register_27_q, register_28_q, register_37_q,
       register_38_q, register_39_q, register_40_q, undriven, undriven_2, undriven_7, undriven_8, undriven_9,
       undriven_10, undriven_11, undriven_12, undriven_13, undriven_14, undriven_15, undriven_16,
       undriven_17, undriven_18;
  wire [3:0] undriven_3, undriven_4, undriven_5, undriven_6;
  wire [15:0] register_5_q, register_6_q, register_7_q, register_8_q, register_9_q, register_10_q,
       register_11_q, register_12_q, register_17_q, register_18_q, register_19_q, register_20_q,
       register_21_q, register_22_q, register_23_q, register_24_q, register_29_q, register_30_q,
       register_31_q, register_32_q, register_33_q, register_34_q, register_35_q, register_36_q,
       register_41_q, register_42_q, register_43_q, register_44_q, register_45_q, register_46_q,
       register_47_q, register_48_q;

  Decoder #(.Selector_Bits(4)) decoder_1 (.sel(IO_InSel));  // open: out_0, out_1, out_2, out_3, out_4, out_5, out_6, out_7, out_8, out_9, out_10, out_11, out_12, out_13, out_14, out_15
  D_FF d_ff_1 (.D(undriven), .C(CLK), .Q(d_ff_1_q));  // open: nQ
  Decoder #(.Selector_Bits(4)) decoder_2 (
    .sel(in_4), .out_0(decoder_2_out_0), .out_1(decoder_2_out_1), .out_2(decoder_2_out_2),
    .out_3(decoder_2_out_3), .out_4(decoder_2_out_4), .out_5(decoder_2_out_5), .out_6(decoder_2_out_6),
    .out_7(decoder_2_out_7), .out_8(decoder_2_out_8), .out_9(decoder_2_out_9), .out_10(decoder_2_out_10),
    .out_11(decoder_2_out_11), .out_12(decoder_2_out_12), .out_13(decoder_2_out_13),
    .out_14(decoder_2_out_14), .out_15(decoder_2_out_15));
  // And and_1 has open pins: In_1=undriven_2, In_2=d_ff_1_q, out=open
  Decoder #(.Selector_Bits(4)) decoder_3 (
    .sel(SetMod_IO[3:0]), .out_0(decoder_3_out_0), .out_1(decoder_3_out_1), .out_2(decoder_3_out_2),
    .out_3(decoder_3_out_3), .out_4(decoder_3_out_4), .out_5(decoder_3_out_5), .out_6(decoder_3_out_6),
    .out_7(decoder_3_out_7), .out_8(decoder_3_out_8), .out_9(decoder_3_out_9), .out_10(decoder_3_out_10),
    .out_11(decoder_3_out_11), .out_12(decoder_3_out_12), .out_13(decoder_3_out_13),
    .out_14(decoder_3_out_14), .out_15(decoder_3_out_15));
  Register register_1 (.D(undriven_3[0]), .C(CLK), .Q(register_1_q));  // open: en
  Register register_2 (.D(undriven_3[1]), .C(CLK), .Q(register_2_q));  // open: en
  Register register_3 (.D(undriven_3[2]), .C(CLK), .Q(register_3_q));  // open: en
  Register register_4 (.D(undriven_3[3]), .C(CLK), .Q(register_4_q));  // open: en
  Register #(.Bits(16)) register_5 (.D(D), .C(CLK), .en(decoder_2_out_0), .Q(register_5_q));
  Register #(.Bits(16)) register_6 (.D(D), .C(CLK), .en(decoder_2_out_1), .Q(register_6_q));
  Register #(.Bits(16)) register_7 (.D(D), .C(CLK), .en(decoder_2_out_2), .Q(register_7_q));
  Register #(.Bits(16)) register_8 (.D(D), .C(CLK), .en(decoder_2_out_3), .Q(register_8_q));
  BlockRAMDualPort #(.Bits(16)) blockramdualport_1 (.A(in_10[1:0]), .Din(D), .str(in_11), .C(CLK), .D(out_12));
  Register #(.Bits(16)) register_9 (.D(D), .C(CLK), .en(decoder_3_out_0), .Q(register_9_q));
  Register #(.Bits(16)) register_10 (.D(D), .C(CLK), .en(decoder_3_out_1), .Q(register_10_q));
  Register #(.Bits(16)) register_11 (.D(D), .C(CLK), .en(decoder_3_out_2), .Q(register_11_q));
  Register #(.Bits(16)) register_12 (.D(D), .C(CLK), .en(decoder_3_out_3), .Q(register_12_q));
  and and_2 (GPIO_OUT0x0, register_1_q, register_9_q[0]);
  and and_3 (GPIO_OUT0x1, register_2_q, register_10_q[0]);
  and and_4 (GPIO_OUT0x2, register_3_q, register_11_q[0]);
  and and_5 (GPIO_OUT0x3, register_4_q, register_12_q[0]);
  Register register_13 (.D(undriven_4[0]), .C(CLK), .en(undriven_10), .Q(register_13_q));
  Register register_14 (.D(undriven_4[1]), .C(CLK), .en(undriven_9), .Q(register_14_q));
  Register register_15 (.D(undriven_4[2]), .C(CLK), .en(undriven_8), .Q(register_15_q));
  Register register_16 (.D(undriven_4[3]), .C(CLK), .en(undriven_7), .Q(register_16_q));
  Register #(.Bits(16)) register_17 (.D(D), .C(CLK), .en(decoder_2_out_4), .Q(register_17_q));
  Register #(.Bits(16)) register_18 (.D(D), .C(CLK), .en(decoder_2_out_5), .Q(register_18_q));
  Register #(.Bits(16)) register_19 (.D(D), .C(CLK), .en(decoder_2_out_6), .Q(register_19_q));
  Register #(.Bits(16)) register_20 (.D(D), .C(CLK), .en(decoder_2_out_7), .Q(register_20_q));
  and and_6 (GPIO_OUT0x4, register_13_q, register_21_q[0]);
  and and_7 (GPIO_OUT0x5, register_14_q, register_22_q[0]);
  and and_8 (GPIO_OUT0x6, register_15_q, register_23_q[0]);
  and and_9 (GPIO_OUT0x7, register_16_q, register_24_q[0]);
  Register #(.Bits(16)) register_21 (.D(D), .C(CLK), .en(decoder_3_out_4), .Q(register_21_q));
  Register #(.Bits(16)) register_22 (.D(D), .C(CLK), .en(decoder_3_out_5), .Q(register_22_q));
  Register #(.Bits(16)) register_23 (.D(D), .C(CLK), .en(decoder_3_out_6), .Q(register_23_q));
  Register #(.Bits(16)) register_24 (.D(D), .C(CLK), .en(decoder_3_out_7), .Q(register_24_q));
  Register register_25 (.D(undriven_5[0]), .C(CLK), .en(undriven_14), .Q(register_25_q));
  Register register_26 (.D(undriven_5[1]), .C(CLK), .en(undriven_13), .Q(register_26_q));
  Register register_27 (.D(undriven_5[2]), .C(CLK), .en(undriven_12), .Q(register_27_q));
  Register register_28 (.D(undriven_5[3]), .C(CLK), .en(undriven_11), .Q(register_28_q));
  Register #(.Bits(16)) register_29 (.D(D), .C(CLK), .en(decoder_2_out_8), .Q(register_29_q));
  Register #(.Bits(16)) register_30 (.D(D), .C(CLK), .en(decoder_2_out_9), .Q(register_30_q));
  Register #(.Bits(16)) register_31 (.D(D), .C(CLK), .en(decoder_2_out_10), .Q(register_31_q));
  Register #(.Bits(16)) register_32 (.D(D), .C(CLK), .en(decoder_2_out_11), .Q(register_32_q));
  and and_10 (GPIO_OUT0x8, register_25_q, register_33_q[0]);
  and and_11 (GPIO_OUT0x9, register_26_q, register_34_q[0]);
  and and_12 (GPIO_OUT0xA, register_27_q, register_35_q[0]);
  and and_13 (GPIO_OUT0xB, register_28_q, register_36_q[0]);
  Register #(.Bits(16)) register_33 (.D(D), .C(CLK), .en(decoder_3_out_8), .Q(register_33_q));
  Register #(.Bits(16)) register_34 (.D(D), .C(CLK), .en(decoder_3_out_9), .Q(register_34_q));
  Register #(.Bits(16)) register_35 (.D(D), .C(CLK), .en(decoder_3_out_10), .Q(register_35_q));
  Register #(.Bits(16)) register_36 (.D(D), .C(CLK), .en(decoder_3_out_11), .Q(register_36_q));
  Register register_37 (.D(undriven_6[0]), .C(CLK), .en(undriven_18), .Q(register_37_q));
  Register register_38 (.D(undriven_6[1]), .C(CLK), .en(undriven_17), .Q(register_38_q));
  Register register_39 (.D(undriven_6[2]), .C(CLK), .en(undriven_16), .Q(register_39_q));
  Register register_40 (.D(undriven_6[3]), .C(CLK), .en(undriven_15), .Q(register_40_q));
  Register #(.Bits(16)) register_41 (.D(D), .C(CLK), .en(decoder_2_out_12), .Q(register_41_q));
  Register #(.Bits(16)) register_42 (.D(D), .C(CLK), .en(decoder_2_out_13), .Q(register_42_q));
  Register #(.Bits(16)) register_43 (.D(D), .C(CLK), .en(decoder_2_out_14), .Q(register_43_q));
  Register #(.Bits(16)) register_44 (.D(D), .C(CLK), .en(decoder_2_out_15), .Q(register_44_q));
  Register #(.Bits(16)) register_45 (.D(D), .C(CLK), .en(decoder_3_out_12), .Q(register_45_q));
  Register #(.Bits(16)) register_46 (.D(D), .C(CLK), .en(decoder_3_out_13), .Q(register_46_q));
  Register #(.Bits(16)) register_47 (.D(D), .C(CLK), .en(decoder_3_out_14), .Q(register_47_q));
  Register #(.Bits(16)) register_48 (.D(D), .C(CLK), .en(decoder_3_out_15), .Q(register_48_q));
  and and_14 (GPIO_OUT0xC, register_37_q, register_45_q[0]);
  and and_15 (GPIO_OUT0xD, register_38_q, register_46_q[0]);
  and and_16 (GPIO_OUT0xE, register_39_q, register_47_q[0]);
  and and_17 (GPIO_OUT0xF, register_40_q, register_48_q[0]);
  Multiplexer #(.Selector_Bits(4)) multiplexer_1 (
    .sel(IO_OutSel), .in_0(register_1_q), .in_1(register_2_q), .in_2(register_3_q), .in_3(register_4_q),
    .in_4(register_13_q), .in_5(register_14_q), .in_6(register_15_q), .in_7(register_16_q),
    .in_8(register_25_q), .in_9(register_26_q), .in_10(register_27_q), .in_11(register_28_q),
    .in_12(register_37_q), .in_13(register_38_q), .in_14(register_39_q), .in_15(register_40_q),
    .out(GPIO_DataOUT));
  Multiplexer #(.Bits(16), .Selector_Bits(4)) multiplexer_2 (
    .sel(in_5), .in_0(register_5_q), .in_1(register_6_q), .in_2(register_7_q), .in_3(register_8_q),
    .in_4(register_17_q), .in_5(register_18_q), .in_6(register_19_q), .in_7(register_20_q),
    .in_8(register_29_q), .in_9(register_30_q), .in_10(register_31_q), .in_11(register_32_q),
    .in_12(register_41_q), .in_13(register_42_q), .in_14(register_43_q), .in_15(register_44_q), .out(out_1));
  // Pins of 2 and 16 bits meet at in_10
  // Pins of 1 and 16 bits meet at out_12
  // Pins of 1 and 16 bits meet at register_9_q
  // Pins of 1 and 16 bits meet at register_10_q
  // Pins of 1 and 16 bits meet at register_11_q
  // Pins of 1 and 16 bits meet at register_12_q
  // Pins of 1 and 16 bits meet at register_21_q
  // Pins of 1 and 16 bits meet at register_22_q
  // Pins of 1 and 16 bits meet at register_23_q
  // Pins of 1 and 16 bits meet at register_24_q
  // Pins of 1 and 16 bits meet at register_33_q
  // Pins of 1 and 16 bits meet at register_34_q
endmodule
